# Fritzing sketch Lesson10 (saved by Fritzing 0.9.3b)
breadboards: 1

parts:
  By_Elegoo = Arduino Uno (Rev3)
  Part2 = SRF05 Ultrasonic Rangefinder

nets:
  N1: By_Elegoo.D11_PWM/MOSI, Part2.Echo
  N2: By_Elegoo.D12/MISO, Part2.Trig
  GND: By_Elegoo.GND, Part2.GND
  5V: By_Elegoo.5V, Part2.VCC

notes:
  Lesson 10 - Ultrasonic Sensor Module
  HC-SR04 will be flipped to face away from the breadboard.
