# Fritzing sketch UltrasonicSensorLCD (saved by Fritzing 0.9.3b)
breadboards: 1

parts:
  By_Elegoo = Arduino Uno (Rev3)
  Module = SRF05 Ultrasonic Rangefinder
  S1 = Pushbutton [package="[THT]"]
  R1 = Rotary Potentiometer (Small) [maximum_resistance=10kΩ package=THT]
  LCD1 = LCD screen

nets:
  N1: By_Elegoo.D9_PWM, LCD1.E
  N2: By_Elegoo.D10_PWM/SS, LCD1.R/W
  N3: By_Elegoo.D11_PWM/MOSI, LCD1.RS
  N4: By_Elegoo.D12/MISO, Module.Echo
  N5: By_Elegoo.D13/SCK, Module.Trig
  N6: By_Elegoo.D2, S1.Pin_1, S1.Pin_2
  N7: By_Elegoo.D3_PWM, LCD1.DB7
  N8: By_Elegoo.D4, LCD1.DB6
  N9: By_Elegoo.D5_PWM, LCD1.DB5
  N10: By_Elegoo.D6_PWM, LCD1.DB4
  5V: By_Elegoo.5V, Module.VCC, R1.leg2, LCD1.VDD, LCD1.LED+
  GND: By_Elegoo.GND, Module.GND, S1.Pin_3, S1.Pin_4, R1.leg1, LCD1.VSS, LCD1.LED-
  N11: R1.wiper, LCD1.V0

notes:
  Ultrasonic Sensor Module with LCD
  HC-SR04 will be flipped to face away from the breadboard.
  Ultrasonic Sensor with LCD
