# Fritzing sketch Keypad_4x4_1analogPin (saved by Fritzing 0.9.3b)
breadboards: 1

parts:
  Keypad_4x4 = Keypad Membran 4x4
  R1 = Resistor [tolerance=±5% resistance=2k package=THT]
  R2 = Resistor [tolerance=±5% resistance=5k package=THT]
  R3 = Resistor [tolerance=±5% resistance=2k package=THT]
  R4 = Resistor [tolerance=±5% resistance=2k package=THT]
  by_Elegoo = Arduino Uno (Rev3)
  R6 = Resistor [tolerance=±5% resistance=330 package=THT]
  R7 = Resistor [tolerance=±5% resistance=330 package=THT]
  R8 = Resistor [tolerance=±5% resistance=330 package=THT]
  C1 = Ceramic Capacitor [capacitance=100nF package="100 mil [THT, multilayer]"]
  R9 = Resistor [tolerance=±5% resistance=2k package=THT]
  R10 = Resistor [tolerance=±5% resistance=100 package=THT]
  R11 = Resistor [tolerance=±5% resistance=100 package=THT]
  R12 = Resistor [tolerance=±5% resistance=100 package=THT]
  R13 = Resistor [tolerance=±5% resistance=220 package=THT]
  R14 = Resistor [tolerance=±5% resistance=220 package=THT]
  R16 = Resistor [tolerance=±5% resistance=330 package=THT]
  R17 = Resistor [tolerance=±5% resistance=220 package=THT]
  R15 = Resistor [tolerance=±5% resistance=220 package=THT]
  R18 = Resistor [tolerance=±5% resistance=100 package=THT]
  R19 = Resistor [tolerance=±5% resistance=10 package=THT]
  R20 = Resistor [tolerance=±5% resistance=10 package=THT]

nets:
  GND: Keypad_4x4.Pin1, R1.Pin_0, by_Elegoo.GND, C1.0
  N1: Keypad_4x4.Pin2, R4.Pin_0, R10.Pin_0
  N2: Keypad_4x4.Pin3, R3.Pin_0, R11.Pin_0
  N3: Keypad_4x4.Pin4, R12.Pin_0
  N4: Keypad_4x4.Pin5, by_Elegoo.A0, R6.Pin_0, C1.1, R20.Pin_1
  N5: Keypad_4x4.Pin6, R7.Pin_0, R15.Pin_0
  N6: Keypad_4x4.Pin7, R8.Pin_0, R14.Pin_0
  N7: Keypad_4x4.Pin8, R13.Pin_0
  N8: R1.Pin_1, R10.Pin_1
  5V: R2.Pin_0, by_Elegoo.5V
  N9: R2.Pin_1, R9.Pin_1
  N10: R3.Pin_1, R12.Pin_1
  N11: R4.Pin_1, R11.Pin_1
  N12: R6.Pin_1, R15.Pin_1
  N13: R7.Pin_1, R14.Pin_1
  N14: R8.Pin_1, R13.Pin_1
  N15: R9.Pin_0, R16.Pin_0
  N16: R16.Pin_1, R17.Pin_1
  N17: R17.Pin_0, R18.Pin_0
  N18: R18.Pin_1, R19.Pin_1
  N19: R19.Pin_0, R20.Pin_0

notes:
  Keypad 4X4 with 1 Analog pin
  R3
  R2
  R1
  R0
  C3
  C2
  C1
  C0
  Resistor Ladder
  7670 Ohms
  550 Ohms
  2100 Ohms
  .1uF or 104
  2100 ohms
  7670 ohms
  550 ohms
  104

custom parts:
  Keypad Membran 4x4: Membrane Keypad 4x4 Matrix
