# Fritzing sketch HC-SR501_plus (saved by Fritzing 0.9.3b)
breadboards: 1

parts:
  Active_Buzzer = Piezo Speaker
  Elegoo = Arduino Uno (Rev3)
  R1 = Resistor [tolerance=±5% resistance=100 package=THT]
  R2 = Resistor [tolerance=±5% resistance=220 package=THT]
  LED1 = LED - 5mm [color="Blue (430nm)" package="5 mm [THT]"]
  LED2 = LED - 5mm [color="Green (555nm)" package="5 mm [THT]"]
  R3 = Resistor [tolerance=±5% resistance=220 package=THT]
  LED3 = LED - 5mm [color="Red (633nm)" package="5 mm [THT]"]
  HC-SR501 = HC-SR501 Body Sensor Module [part_number="PIR Sensor"]
  R4 = Resistor [tolerance=±5% resistance=220 package=THT]

nets:
  GND: Active_Buzzer.pin1, Elegoo.GND, LED1.cathode, LED2.cathode, LED3.cathode, HC-SR501.GND
  N1: Active_Buzzer.pin2, R1.Pin_0
  N2: Elegoo.D8, R4.Pin_1
  N3: Elegoo.D9_PWM, R3.Pin_1
  N4: Elegoo.D10_PWM/SS, R2.Pin_1
  N5: Elegoo.D11_PWM/MOSI, R1.Pin_1
  N6: Elegoo.D7, HC-SR501.OUT
  5V: Elegoo.5V, HC-SR501.VCC
  N7: R2.Pin_0, LED1.anode
  N8: LED2.anode, R3.Pin_0
  N9: LED3.anode, R4.Pin_0

notes:
  5V
  OUT
  GND
  HC-SR501 PIR Sensor Sketch

custom parts:
  HC-SR501 Body Sensor Module: Pyroelectric Infrared PIR Motion Sensor Detector Module
