# Fritzing sketch Lesson20 (saved by Fritzing 0.9.3b)

parts:
  Part2 = Elegoo Arduino Uno (Rev3)
  KY2 = KY-038 Sound Sensor Module

nets:
  N1: Part2.A0, KY2.AO
  GND: Part2.GND, KY2.G
  N2: Part2.D3_PWM, KY2.D0
  5V: Part2.5V, KY2.VCC

notes:
  Lesson 20
  Sound Sensor Module

custom parts:
  Elegoo Arduino Uno (Rev3): The Arduino Uno is a microcontroller board based on the ATmega328 (datasheet). It has 14 digital input/output pins (of which 6 can be used as PWM outputs), 6 analog inputs, a 16 MHz ceramic resonator, a USB connection, a power jack, an ICSP header, and a reset button. It contains everything needed to support the microcontroller; simply connect it to a computer with a USB cable or power it with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
