# Fritzing sketch SoundSensor (saved by Fritzing 0.9.3b)
breadboards: 1

parts:
  Part2 = Elegoo Arduino Uno (Rev3)
  KY2 = KY-038 Sound Sensor Module
  R1 = Resistor [tolerance=±5% resistance=330 package=THT]
  Part3 = OLED Monochrome 128x64 1.3 inch [part_number=938]
  LED1 = LED - 5mm [color="Red (633nm)" package="5 mm [THT]"]

nets:
  N1: Part2.A0, KY2.AO
  N2: Part2.D8, Part3.RESET
  N3: Part2.D11_PWM/MOSI, Part3.MOSI_SDA
  N4: Part2.D13/SCK, Part3.SCLK_SCK
  N5: Part2.D3_PWM, KY2.D0
  N6: Part2.D5_PWM, R1.Pin_0
  N7: Part2.D6_PWM, Part3.CS
  N8: Part2.D7, Part3.DC_SA0
  5V: Part2.5V, KY2.VCC, Part3.VIN
  GND: Part2.GND, KY2.G, Part3.GND, LED1.cathode
  N9: R1.Pin_1, LED1.anode

notes:
  Lesson 20
  Sound Sensor Calibrator & LED switch

custom parts:
  Elegoo Arduino Uno (Rev3): The Arduino Uno is a microcontroller board based on the ATmega328 (datasheet). It has 14 digital input/output pins (of which 6 can be used as PWM outputs), 6 analog inputs, a 16 MHz ceramic resonator, a USB connection, a power jack, an ICSP header, and a reset button. It contains everything needed to support the microcontroller; simply connect it to a computer with a USB cable or power it with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
  OLED Monochrome 128x64 1.3 inch: These displays are small, only about 1.3" diagonal, but very readable due to the high contrast of an OLED display. This display is made of 128x64 individual white OLED pixels, each one is turned on or off by the controller chip. Because the display makes its own light, no backlight is required. This reduces the power required to run the OLED and is why the display has such high contrast; we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
