# Fritzing sketch LCD1602A_I2C (saved by Fritzing 0.9.3b)
breadboards: 1

parts:
  Part1 = Elegoo Arduino Uno (Rev3)
  LCD1 = LCD screen
  LCM1602_IIC2 = LCM1602 IIC [part_number="LCM1602 IIC" chip_label="LCM1602 IIC" package="DIP (Dual Inline) [THT]"]

nets:
  SDA: Part1.A4/SDA, LCM1602_IIC2.SDA
  SCL: Part1.A5/SCL, LCM1602_IIC2.SCL
  5V: Part1.5V, LCM1602_IIC2.VCC
  GND: Part1.GND, LCM1602_IIC2.GND
  VSS: LCD1.VSS, LCM1602_IIC2.VSS
  VDD: LCD1.VDD, LCM1602_IIC2.VDD
  N1: LCD1.V0, LCM1602_IIC2.V0
  N2: LCD1.RS, LCM1602_IIC2.RS
  N3: LCD1.R/W, LCM1602_IIC2.RW
  N4: LCD1.E, LCM1602_IIC2.E
  N5: LCD1.DB0, LCM1602_IIC2.D0
  N6: LCD1.DB1, LCM1602_IIC2.D1
  N7: LCD1.DB2, LCM1602_IIC2.D2
  N8: LCD1.DB3, LCM1602_IIC2.D3
  N9: LCD1.DB4, LCM1602_IIC2.D4
  N10: LCD1.DB5, LCM1602_IIC2.D5
  N11: LCD1.DB6, LCM1602_IIC2.D6
  N12: LCD1.DB7, LCM1602_IIC2.D7
  N13: LCD1.LED+, LCM1602_IIC2.A
  N14: LCD1.LED-, LCM1602_IIC2.K
  N15: LCM1602_IIC2.LED_A, LCM1602_IIC2.LED_B

notes:
  K
  A
  Lesson 22 - 1602A LCD Module w/I2C
  GND
  +5V

custom parts:
  Elegoo Arduino Uno (Rev3): The Arduino Uno is a microcontroller board based on the ATmega328 (datasheet). It has 14 digital input/output pins (of which 6 can be used as PWM outputs), 6 analog inputs, a 16 MHz ceramic resonator, a USB connection, a power jack, an ICSP header, and a reset button. It contains everything needed to support the microcontroller; simply connect it to a computer with a USB cable or power it with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
  LCM1602 IIC: I2C-Module to use a 1602 or 2004 LCD on with the wire.h libory Serial LCD Modul
