# Fritzing sketch Thermistor (saved by Fritzing 0.9.3b)
breadboards: 1

parts:
  Part1 = Elegoo Arduino Uno (Rev3)
  LCD1 = LCD screen
  R2 = Trimmer Potentiometer [maximum_resistance=10kΩ package=THT]
  R1 = Resistor [tolerance=±5% resistance=220 package=THT]
  R3 = Temperature Sensor (Thermistor) [thermistor_type=NTC package=THT]
  R4 = Resistor [tolerance=±5% resistance=10k package=THT]

nets:
  N1: Part1.A0, R3.pin_0, R4.Pin_0
  N2: Part1.D11_PWM/MOSI, LCD1.E
  N3: Part1.D12/MISO, LCD1.RS
  N4: Part1.D2, LCD1.DB7
  N5: Part1.D3_PWM, LCD1.DB6
  N6: Part1.D4, LCD1.DB5
  N7: Part1.D5_PWM, LCD1.DB4
  5V: Part1.5V, LCD1.VDD, R2.leg2, R1.Pin_1, R3.pin_1
  GND: Part1.GND, LCD1.VSS, LCD1.R/W, LCD1.LED-, R2.leg1, R4.Pin_1
  N8: LCD1.V0, R2.wiper
  N9: LCD1.LED+, R1.Pin_0

notes:
  K
  A
  Lesson 23 - Thermometer
  GND
  +5V

custom parts:
  Elegoo Arduino Uno (Rev3): The Arduino Uno is a microcontroller board based on the ATmega328 (datasheet). It has 14 digital input/output pins (of which 6 can be used as PWM outputs), 6 analog inputs, a 16 MHz ceramic resonator, a USB connection, a power jack, an ICSP header, and a reset button. It contains everything needed to support the microcontroller; simply connect it to a computer with a USB cable or power it with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
