# Fritzing sketch B2B_74HC595 (saved by Fritzing 0.9.3b)
breadboards: 1

parts:
  Part1 = Elegoo Arduino Uno (Rev3)
  U1 = 74HC595 [package="DIP16 [THT]"]
  LED1 = LED - 5mm [color="Blue (430nm)" package="5 mm [THT]"]
  LED2 = LED - 5mm [color="Blue (430nm)" package="5 mm [THT]"]
  LED3 = LED - 5mm [color="Yellow (595nm)" package="5 mm [THT]"]
  LED4 = LED - 5mm [color="Yellow (595nm)" package="5 mm [THT]"]
  LED5 = LED - 5mm [color="Red (633nm)" package="5 mm [THT]"]
  LED6 = LED - 5mm [color="Red (633nm)" package="5 mm [THT]"]
  LED7 = LED - 5mm [color="Green (555nm)" package="5 mm [THT]"]
  LED8 = LED - 5mm [color="Green (555nm)" package="5 mm [THT]"]
  R7 = Resistor [tolerance=±5% resistance=220 package=THT]
  R6 = Resistor [tolerance=±5% resistance=220 package=THT]
  R5 = Resistor [tolerance=±5% resistance=220 package=THT]
  R4 = Resistor [tolerance=±5% resistance=220 package=THT]
  R3 = Resistor [tolerance=±5% resistance=220 package=THT]
  R2 = Resistor [tolerance=±5% resistance=220 package=THT]
  R1 = Resistor [tolerance=±5% resistance=220 package=THT]
  R0 = Resistor [tolerance=±5% resistance=220 package=THT]
  U2 = 74HC595 [package="DIP16 [THT]"]
  LED9 = LED - 5mm [color="Green (555nm)" package="5 mm [THT]"]
  LED10 = LED - 5mm [color="Green (555nm)" package="5 mm [THT]"]
  LED11 = LED - 5mm [color="Red (633nm)" package="5 mm [THT]"]
  LED12 = LED - 5mm [color="Red (633nm)" package="5 mm [THT]"]
  LED13 = LED - 5mm [color="Blue (430nm)" package="5 mm [THT]"]
  LED14 = LED - 5mm [color="Blue (430nm)" package="5 mm [THT]"]
  LED15 = LED - 5mm [color="Yellow (595nm)" package="5 mm [THT]"]
  LED16 = LED - 5mm [color="Yellow (595nm)" package="5 mm [THT]"]
  R8 = Resistor [tolerance=±5% resistance=220 package=THT]
  R9 = Resistor [tolerance=±5% resistance=220 package=THT]
  R10 = Resistor [tolerance=±5% resistance=220 package=THT]
  R11 = Resistor [tolerance=±5% resistance=220 package=THT]
  R12 = Resistor [tolerance=±5% resistance=220 package=THT]
  R13 = Resistor [tolerance=±5% resistance=220 package=THT]
  R14 = Resistor [tolerance=±5% resistance=220 package=THT]
  R15 = Resistor [tolerance=±5% resistance=220 package=THT]

nets:
  N1: Part1.D9_PWM, U1.SH_CP, U2.SH_CP
  N2: Part1.D11_PWM/MOSI, U1.ST_CP, U2.ST_CP
  N3: Part1.D12/MISO, U1.DS
  5V: Part1.5V, U1.MR, U1.VCC, U2.MR, U2.VCC
  GND: Part1.GND, U1.GND, U1.OE, LED1.cathode, LED2.cathode, LED3.cathode, LED4.cathode, LED5.cathode, LED6.cathode, LED7.cathode, LED8.cathode, U2.GND, U2.OE, LED9.cathode, LED10.cathode, LED11.cathode, LED12.cathode, LED13.cathode, LED14.cathode, LED15.cathode, LED16.cathode
  N4: U1.Q1, R1.Pin_1
  N5: U1.Q2, R2.Pin_1
  N6: U1.Q3, R3.Pin_1
  N7: U1.Q4, R4.Pin_1
  N8: U1.Q5, R5.Pin_1
  N9: U1.Q6, R6.Pin_1
  N10: U1.Q7, R7.Pin_1
  N11: U1.Q7', U2.DS
  N12: U1.Q0, R0.Pin_1
  N13: LED1.anode, R13.Pin_0
  N14: LED2.anode, R12.Pin_0
  N15: LED3.anode, R9.Pin_0
  N16: LED4.anode, R8.Pin_0
  N17: LED5.anode, R5.Pin_0
  N18: LED6.anode, R4.Pin_0
  N19: LED7.anode, R1.Pin_0
  N20: LED8.anode, R0.Pin_0
  N21: R7.Pin_0, LED12.anode
  N22: R6.Pin_0, LED11.anode
  N23: R3.Pin_0, LED10.anode
  N24: R2.Pin_0, LED9.anode
  N25: U2.Q1, R9.Pin_1
  N26: U2.Q2, R10.Pin_1
  N27: U2.Q3, R11.Pin_1
  N28: U2.Q4, R12.Pin_1
  N29: U2.Q5, R13.Pin_1
  N30: U2.Q6, R14.Pin_1
  N31: U2.Q7, R15.Pin_1
  N32: U2.Q0, R8.Pin_1
  N33: LED13.anode, R15.Pin_0
  N34: LED14.anode, R14.Pin_0
  N35: LED15.anode, R10.Pin_0
  N36: LED16.anode, R11.Pin_0

notes:
  Lesson 24 - B2B Shift Register 74HC595

custom parts:
  Elegoo Arduino Uno (Rev3): The Arduino Uno is a microcontroller board based on the ATmega328 (datasheet). It has 14 digital input/output pins (of which 6 can be used as PWM outputs), 6 analog inputs, a 16 MHz ceramic resonator, a USB connection, a power jack, an ICSP header, and a reset button. It contains everything needed to support the microcontroller; simply connect it to a computer with a USB cable or power it with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
