# Fritzing sketch PhotoCell (saved by Fritzing 0.9.3b)
breadboards: 1

parts:
  Part1 = Elegoo Arduino Uno (Rev3)
  U1 = 74HC595 [package="DIP16 [THT]"]
  LED1 = LED - 5mm [color="Blue (430nm)" package="5 mm [THT]"]
  LED2 = LED - 5mm [color="Blue (430nm)" package="5 mm [THT]"]
  LED3 = LED - 5mm [color="Yellow (595nm)" package="5 mm [THT]"]
  LED4 = LED - 5mm [color="Yellow (595nm)" package="5 mm [THT]"]
  LED5 = LED - 5mm [color="Red (633nm)" package="5 mm [THT]"]
  LED6 = LED - 5mm [color="Red (633nm)" package="5 mm [THT]"]
  LED7 = LED - 5mm [color="Green (555nm)" package="5 mm [THT]"]
  LED8 = LED - 5mm [color="Green (555nm)" package="5 mm [THT]"]
  R7 = Resistor [tolerance=±5% resistance=220 package=THT]
  R6 = Resistor [tolerance=±5% resistance=220 package=THT]
  R5 = Resistor [tolerance=±5% resistance=220 package=THT]
  R4 = Resistor [tolerance=±5% resistance=220 package=THT]
  R3 = Resistor [tolerance=±5% resistance=220 package=THT]
  R2 = Resistor [tolerance=±5% resistance=220 package=THT]
  R1 = Resistor [tolerance=±5% resistance=220 package=THT]
  R0 = Resistor [tolerance=±5% resistance=220 package=THT]
  R8 = Photocell (LDR) [package=THT]
  R9 = Resistor [tolerance=±5% resistance=1k package=THT]

nets:
  N1: Part1.A0, R8.pin_0, R9.Pin_1
  N2: Part1.D9_PWM, U1.SH_CP
  N3: Part1.D11_PWM/MOSI, U1.ST_CP
  N4: Part1.D12/MISO, U1.DS
  5V: Part1.5V, U1.MR, U1.VCC, R8.pin_1
  GND: Part1.GND, U1.GND, U1.OE, LED1.cathode, LED2.cathode, LED3.cathode, LED4.cathode, LED5.cathode, LED6.cathode, LED7.cathode, LED8.cathode, R9.Pin_0
  N5: U1.Q1, R1.Pin_1
  N6: U1.Q2, R2.Pin_1
  N7: U1.Q3, R3.Pin_1
  N8: U1.Q4, R4.Pin_1
  N9: U1.Q5, R5.Pin_1
  N10: U1.Q6, R6.Pin_1
  N11: U1.Q7, R7.Pin_1
  N12: U1.Q0, R0.Pin_1
  N13: LED1.anode, R7.Pin_0
  N14: LED2.anode, R6.Pin_0
  N15: LED3.anode, R5.Pin_0
  N16: LED4.anode, R4.Pin_0
  N17: LED5.anode, R3.Pin_0
  N18: LED6.anode, R2.Pin_0
  N19: LED7.anode, R1.Pin_0
  N20: LED8.anode, R0.Pin_0

notes:
  Lesson 26 - Photocell

custom parts:
  Elegoo Arduino Uno (Rev3): The Arduino Uno is a microcontroller board based on the ATmega328 (datasheet). It has 14 digital input/output pins (of which 6 can be used as PWM outputs), 6 analog inputs, a 16 MHz ceramic resonator, a USB connection, a power jack, an ICSP header, and a reset button. It contains everything needed to support the microcontroller; simply connect it to a computer with a USB cable or power it with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
