# Fritzing sketch 74HC595_7SegmentDisplay (saved by Fritzing 0.9.3b)
breadboards: 1

parts:
  Part1 = Elegoo Arduino Uno (Rev3)
  U1 = 74HC595 [package="DIP16 [THT]"]
  R0 = Resistor [tolerance=±5% resistance=220 package=THT]
  R1 = Resistor [tolerance=±5% resistance=220 package=THT]
  R6 = Resistor [tolerance=±5% resistance=220 package=THT]
  R7 = Resistor [tolerance=±5% resistance=220 package=THT]
  R2 = Resistor [tolerance=±5% resistance=220 package=THT]
  R3 = Resistor [tolerance=±5% resistance=220 package=THT]
  R5 = Resistor [tolerance=±5% resistance=220 package=THT]
  U2 = 7-SEGMENT-DISPLAY [package=7-segment-display]
  R4 = Resistor [tolerance=±5% resistance=220 package=THT]

nets:
  N1: Part1.D9_PWM, U1.SH_CP
  N2: Part1.D11_PWM/MOSI, U1.ST_CP
  N3: Part1.D12/MISO, U1.DS
  5V: Part1.5V, U1.MR, U1.VCC
  GND: Part1.GND, U1.GND, U1.OE, U2.C, U2.F
  N4: U1.Q1, R1.Pin_0
  N5: U1.Q2, R2.Pin_0
  N6: U1.Q3, R3.Pin_0
  N7: U1.Q4, R4.Pin_1
  N8: U1.Q5, R5.Pin_0
  N9: U1.Q6, R6.Pin_0
  N10: U1.Q7, R7.Pin_0
  N11: U1.Q0, R0.Pin_0
  N12: R0.Pin_1, U2.A
  N13: R1.Pin_1, U2.G2
  N14: R6.Pin_1, U2.G
  N15: R7.Pin_1, U2.E
  N16: R2.Pin_1, U2.B
  N17: R3.Pin_1, U2.DP
  N18: R5.Pin_1, U2.D
  N19: U2.G1, R4.Pin_0

notes:
  Lesson 27 - 74HC595 & 7-Segment Display
  Lesson 27 -  74HC595 & 7-Segment Display

custom parts:
  Elegoo Arduino Uno (Rev3): The Arduino Uno is a microcontroller board based on the ATmega328 (datasheet). It has 14 digital input/output pins (of which 6 can be used as PWM outputs), 6 analog inputs, a 16 MHz ceramic resonator, a USB connection, a power jack, an ICSP header, and a reset button. It contains everything needed to support the microcontroller; simply connect it to a computer with a USB cable or power it with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
