# Fritzing sketch DC_Motor (saved by Fritzing 0.9.3b)
breadboards: 1

parts:
  YwRobot_Power_Supply1 = YwRobot Breadboard Power Supply [part_number=545043]
  M1 = DC Motor
  IC1 = L293D [package=THT]
  C1 = Ceramic Capacitor [capacitance=100nF package="100 mil [THT, multilayer]"]
  C2 = Ceramic Capacitor [capacitance=1µF package="100 mil [THT, multilayer]"]
  Part1 = Elegoo Arduino Uno (Rev3)

nets:
  5V: YwRobot_Power_Supply1.VCC, IC1.+Vmotor, IC1.+V, C1.0, C2.1
  GND: YwRobot_Power_Supply1.GND, IC1.0V, C1.1, C2.0, Part1.GND
  N1: M1.pin_1, IC1.Out_1_(_Controlled_by_Enable_1_)
  N2: M1.pin_2, IC1.Out_2_(_Controlled_by_Enable_1_)
  N3: IC1.Enable_1, Part1.D5_PWM
  N4: IC1.In_1, Part1.D4
  N5: IC1.In_2, Part1.D3_PWM

notes:
  Lesson 29 - DC Motors

custom parts:
  YwRobot Breadboard Power Supply: The YwRobot Breadboard Power Supply (MB-V2) has two power rails; they can be 5V or 3V3. Power to the module can be provided through the female USB socket or through the A10 (female) 2.1mm power jack.
  Elegoo Arduino Uno (Rev3): The Arduino Uno is a microcontroller board based on the ATmega328 (datasheet). It has 14 digital input/output pins (of which 6 can be used as PWM outputs), 6 analog inputs, a 16 MHz ceramic resonator, a USB connection, a power jack, an ICSP header, and a reset button. It contains everything needed to support the microcontroller; simply connect it to a computer with a USB cable or power it with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
