# Fritzing sketch Lesson 5 Single Button Sketch (saved by Fritzing 0.9.3b)
breadboards: 1

parts:
  by_Elegoo = Arduino Uno (Rev3)
  LED1 = LED - 5mm [color="Red (633nm)" package="5 mm [THT]"]
  R1 = Resistor [tolerance=±5% resistance=220 package=THT]
  S1 = Pushbutton [package="[THT]"]

nets:
  N1: by_Elegoo.GND, LED1.cathode, S1.Pin_1, S1.Pin_2
  N2: by_Elegoo.D2, S1.Pin_3, S1.Pin_4
  N3: by_Elegoo.D5_PWM, R1.Pin_1
  N4: LED1.anode, R1.Pin_0

notes:
  Lesson 5 - Digital Input with Debounce
  220 Ohms (Red, Red, Black, Black)
