# Fritzing sketch Lesson 5 Sketch (saved by Fritzing 0.9.3b)
breadboards: 1

parts:
  by_Elegoo = Arduino Uno (Rev3)
  LED1 = LED - 5mm [color="Red (633nm)" package="5 mm [THT]"]
  R1 = Resistor [tolerance=±5% resistance=220 package=THT]
  S1 = Pushbutton [package="[THT]"]
  S2 = Pushbutton [package="[THT]"]

nets:
  N1: by_Elegoo.D8, S1.Pin_3, S1.Pin_4
  N2: by_Elegoo.D9_PWM, S2.Pin_3, S2.Pin_4
  N3: by_Elegoo.GND, LED1.cathode, S1.Pin_1, S1.Pin_2, S2.Pin_1, S2.Pin_2
  N4: by_Elegoo.D5_PWM, R1.Pin_1
  N5: LED1.anode, R1.Pin_0

notes:
  Lesson 5 - Digital Inputs
  220 Ohms (Red, Red, Black, Black)
