# Fritzing sketch Lesson 6 (saved by Fritzing 0.9.3b)
breadboards: 1

parts:
  by_Elegoo = Arduino Uno (Rev3)
  Active_Buzzer = Piezo Speaker

nets:
  N1: by_Elegoo.D12/MISO, Active_Buzzer.pin2
  N2: by_Elegoo.GND, Active_Buzzer.pin1

notes:
  Leson 6 - Active Buzzer
  +
  Lesson 6 - Active Buzzer
