# Fritzing sketch Morse Code Translator (saved by Fritzing 0.9.3b)
breadboards: 1

parts:
  by_Elegoo = Arduino Uno (Rev3)
  Active_Buzzer = Piezo Speaker
  LED1 = LED - 5mm [color="Red (633nm)" package="5 mm [THT]"]
  R1 = Resistor [tolerance=±5% resistance=220 package=THT]
  R2 = Resistor [tolerance=±5% resistance=150 package=THT]

nets:
  N1: by_Elegoo.D12/MISO, R2.Pin_1
  N2: by_Elegoo.GND, Active_Buzzer.pin1, LED1.cathode
  N3: by_Elegoo.D6_PWM, R1.Pin_1
  N4: Active_Buzzer.pin2, R2.Pin_0
  N5: LED1.anode, R1.Pin_0

notes:
  Leson 6 - Active Buzzer
  +
  Lesson 6 - Active Buzzer
