# Fritzing sketch Lesson7 (saved by Fritzing 0.9.3b)
breadboards: 1

parts:
  J1 = Piezo Speaker
  by_Elegoo = Arduino Uno (Rev3)
  D1 = Rectifier Diode [part_number=1N4007 package="300 mil [THT]"]
  R1 = Resistor [tolerance=±5% resistance=100 package=THT]

nets:
  N1: J1.pin1, by_Elegoo.GND, D1.anode
  N2: J1.pin2, D1.cathode, R1.Pin_0
  N3: by_Elegoo.D8, R1.Pin_1

notes:
  Lesson 7 - Passive Buzzer
  100ohm resistor
  Passive Buzzer
  +
