# Fritzing sketch MusicPlayer (saved by Fritzing 0.9.3b)
breadboards: 1

parts:
  By_Elegoo = Arduino Uno (Rev3)
  J1 = Piezo Speaker
  LED1 = LED - 5mm [color="Red (633nm)" package="5 mm [THT]"]
  D1 = Rectifier Diode [part_number=1N4007 package="300 mil [THT]"]
  R1 = Resistor [tolerance=±5% resistance=220 package=THT]
  LED2 = LED - 5mm [color="Yellow (595nm)" package="5 mm [THT]"]
  D2 = Rectifier Diode [part_number=1N4007 package="300 mil [THT]"]
  J2 = Piezo Speaker
  R3 = Resistor [tolerance=±5% resistance=100 package=THT]
  LED3 = LED - 5mm [color="Green (560nm)" package="5 mm [THT]"]
  D3 = Rectifier Diode [part_number=1N4001 package="300 mil [THT]"]
  R4 = Resistor [tolerance=±5% resistance=100 package=THT]
  J3 = Piezo Speaker
  R5 = Resistor [tolerance=±5% resistance=220 package=THT]
  R6 = Resistor [tolerance=±5% resistance=220 package=THT]
  R2 = Resistor [tolerance=±5% resistance=100 package=THT]

nets:
  N1: By_Elegoo.A0, R6.Pin_0
  N2: By_Elegoo.A3, R5.Pin_0
  N3: By_Elegoo.A5/SCL, R1.Pin_0
  N4: By_Elegoo.D12/MISO, R4.Pin_1
  N5: By_Elegoo.GND, J1.pin1, LED1.cathode, D1.anode, LED2.cathode, D2.anode, J2.pin1, LED3.cathode, D3.anode, J3.pin1
  N6: By_Elegoo.D2, R3.Pin_1
  N7: By_Elegoo.D6_PWM, R2.Pin_1
  N8: J1.pin2, D1.cathode, R3.Pin_0
  N9: LED1.anode, R6.Pin_1
  N10: R1.Pin_1, LED3.anode
  N11: LED2.anode, R5.Pin_1
  N12: D2.cathode, J2.pin2, R4.Pin_0
  N13: D3.cathode, J3.pin2, R2.Pin_0

notes:
  Lesson 7 - Passive Buzzer and Music Player
  B1
  B2
  B3
  100ohm resistors
  220ohm resistors
  +
