# Fritzing sketch MusicPlayer2 (saved by Fritzing 0.9.3b)
breadboards: 1

parts:
  by_Elegoo = Arduino Uno (Rev3)
  J1 = Piezo Speaker
  J2 = Piezo Speaker
  J3 = Piezo Speaker
  R1 = Resistor [tolerance=±5% resistance=100 package=THT]
  R2 = Resistor [tolerance=±5% resistance=100 package=THT]
  R3 = Resistor [tolerance=±5% resistance=100 package=THT]
  D1 = Rectifier Diode [part_number=1N4007 package="300 mil [THT]"]
  LED1 = LED - 5mm [color="Red (633nm)" package="5 mm [THT]"]
  D2 = Rectifier Diode [part_number=1N4007 package="300 mil [THT]"]
  D3 = Rectifier Diode [part_number=1N4007 package="300 mil [THT]"]
  LED2 = LED - 5mm [color="Yellow (585nm)" package="5 mm [THT]"]
  LED3 = LED - 5mm [color="Green (560nm)" package="5 mm [THT]"]
  R4 = Resistor [tolerance=±5% resistance=220 package=THT]
  R5 = Resistor [tolerance=±5% resistance=220 package=THT]
  R6 = Resistor [tolerance=±5% resistance=220 package=THT]

nets:
  N1: by_Elegoo.A0, R6.Pin_1
  N2: by_Elegoo.A3, R5.Pin_1
  N3: by_Elegoo.A5/SCL, R4.Pin_1
  N4: by_Elegoo.D12/MISO, R1.Pin_0
  N5: by_Elegoo.GND, J1.pin1, J2.pin1, J3.pin1, D1.anode, LED1.cathode, D2.anode, D3.anode, LED2.cathode, LED3.cathode
  N6: by_Elegoo.D2, R3.Pin_0
  N7: by_Elegoo.D6_PWM, R2.Pin_0
  N8: J1.pin2, R1.Pin_1, D1.cathode
  N9: J2.pin2, R2.Pin_1, D2.cathode
  N10: J3.pin2, R3.Pin_1, D3.cathode
  N11: LED1.anode, R6.Pin_0
  N12: LED2.anode, R5.Pin_0
  N13: LED3.anode, R4.Pin_0

notes:
  Lesson 7 - Music Player
  +
  100ohms
  220ohms
  Passive Buzzer
  Yes, the Diodes are connected correctly
  Diode's stripe should be pointed towards the positive pin of the buzzer. It looks backwards, but it's OK.
