# Fritzing sketch Magic8-Ball (saved by Fritzing 0.9.3b)
breadboards: 1

parts:
  by_Elegoo = Arduino Uno (Rev3)
  LCD1602 = LCD screen
  Tilt_Sensor = Tilt Switch [package=THT]
  R1 = Trimmer Potentiometer [maximum_resistance=10kΩ package=THT]

nets:
  N1: by_Elegoo.D10_PWM/SS, LCD1602.E
  N2: by_Elegoo.D11_PWM/MOSI, LCD1602.R/W
  N3: by_Elegoo.D12/MISO, LCD1602.RS
  N4: by_Elegoo.D2, LCD1602.DB7
  N5: by_Elegoo.D3_PWM, LCD1602.DB6
  N6: by_Elegoo.D4, LCD1602.DB5
  N7: by_Elegoo.D5_PWM, LCD1602.DB4
  N8: by_Elegoo.D6_PWM, Tilt_Sensor.Pin_1
  5V: by_Elegoo.5V, LCD1602.VDD, LCD1602.LED+, R1.leg1
  GND: by_Elegoo.GND, LCD1602.LED-, Tilt_Sensor.Pin_2
  N9: LCD1602.VSS, R1.leg2
  N10: LCD1602.V0, R1.wiper

notes:
  Lesson 8 - Tilt Ball Switch and Magic 8-Ball
  Vss Vdd V0 RS RW E DB0 DB1 DB2 DB3 DB4 DB5 DB6 DB7 A K
