# Fritzing sketch Lesson 9 Servo_RotaryEncoder (saved by Fritzing 0.9.3b)
breadboards: 1

parts:
  By_Elegoo = Arduino Uno (Rev3)
  SG90 = Basic Servo
  Rotary_Encoder = Rotary Encoder [package=THT]
  RGB_LED = RGB LED (com. cathode, rgb) [package="5 mm [THT]"]
  NoName_1_3inch_OLED_128x64 = WaveShare 1.3inch OLED 128x64
  C1 = Ceramic Capacitor [capacitance=22pF package="100 mil [THT, multilayer]"]
  C2 = Ceramic Capacitor [capacitance=22pF package="100 mil [THT, multilayer]"]
  R1 = Resistor [tolerance=±5% resistance=220 package=THT]
  R2 = Resistor [tolerance=±5% resistance=220 package=THT]
  R3 = Resistor [tolerance=±5% resistance=220 package=THT]
  R4 = Resistor [tolerance=±5% resistance=10k package=THT]
  R5 = Resistor [tolerance=±5% resistance=10k package=THT]
  R6 = Resistor [tolerance=±5% resistance=10k package=THT]
  R7 = Resistor [tolerance=±5% resistance=10k package=THT]
  C3 = Ceramic Capacitor [capacitance=0.1µF package="100 mil [THT, multilayer]"]
  Encoder_Button = Pushbutton [package=THT]
  R8 = Resistor [tolerance=±5% resistance=10k package=THT]
  R9 = Resistor [tolerance=±5% resistance=10k package=THT]

nets:
  N1: By_Elegoo.A0, C2.1, R5.Pin_0
  N2: By_Elegoo.A1, C1.1, R4.Pin_0
  N3: By_Elegoo.D9_PWM, NoName_1_3inch_OLED_128x64.CS
  N4: By_Elegoo.D10_PWM/SS, NoName_1_3inch_OLED_128x64.D/C
  N5: By_Elegoo.D11_PWM/MOSI, NoName_1_3inch_OLED_128x64.RES
  N6: By_Elegoo.D12/MISO, NoName_1_3inch_OLED_128x64.DIN
  N7: By_Elegoo.D13/SCK, NoName_1_3inch_OLED_128x64.CLK
  GND: By_Elegoo.GND, SG90.gnd, Rotary_Encoder.EncoderPinC, RGB_LED.common_cathode, NoName_1_3inch_OLED_128x64.GND, C1.0, C2.0, C3.0, Encoder_Button.leg0
  N8: By_Elegoo.D2, SG90.pulse
  N9: By_Elegoo.D3_PWM, R6.Pin_0, C3.1
  N10: By_Elegoo.D5_PWM, R3.Pin_0
  N11: By_Elegoo.D6_PWM, R2.Pin_0
  N12: By_Elegoo.D7, R1.Pin_0
  5V: By_Elegoo.5V, SG90.vcc, NoName_1_3inch_OLED_128x64.VCC, R7.Pin_0
  N13: Rotary_Encoder.EncoderPinA, R4.Pin_1, R8.Pin_0
  N14: Rotary_Encoder.EncoderPinB, R5.Pin_1, R9.Pin_1
  N15: RGB_LED.red_anode, R1.Pin_1
  N16: RGB_LED.green_anode, R2.Pin_1
  N17: RGB_LED.blue_anode, R3.Pin_1
  N18: R6.Pin_1, Encoder_Button.leg1
  N19: R7.Pin_1, R8.Pin_1, R9.Pin_0

notes:
  Lesson 9 - Rotary Encoder Servo Adjuster
  Pull-Up Resistors
  Keyes KY-40
  Pin A
  Pin B

custom parts:
  WaveShare 1.3inch OLED 128x64: OLED Original design by Simulz (http://tsblog.simulz.kr) Corrected PCB layout by Andreas Horneffer
