# Fritzing sketch Lesson4 (saved by Fritzing 0.9.3b)
breadboards: 1

parts:
  Lesson_4 = Arduino Uno (Rev3)
  RGB_LED1 = RGB LED (com. cathode, rgb) [package="5 mm [THT]"]
  R1 = Resistor [tolerance=±5% resistance=220 package=THT]
  R2 = Resistor [tolerance=±5% resistance=220 package=THT]
  R3 = Resistor [tolerance=±5% resistance=220 package=THT]

nets:
  N1: Lesson_4.GND, RGB_LED1.common_cathode
  N2: Lesson_4.D3_PWM, R3.Pin_0
  N3: Lesson_4.D5_PWM, R2.Pin_0
  N4: Lesson_4.D6_PWM, R1.Pin_0
  N5: RGB_LED1.red_anode, R1.Pin_1
  N6: RGB_LED1.green_anode, R2.Pin_1
  N7: RGB_LED1.blue_anode, R3.Pin_1
